// Digital circuit ponderada_4_bits.dig as structural Verilog
module ponderada_4_bits (
  input  in_1,
  input  in_2,
  input  in_3,
  input  in_6,
  input  in_7,
  input  in_8,
  input  in_10,
  input  in_11,
  input  in_13,
  input  in_14,
  input  in_16,
  input  in_17,
  output out_4,
  output out_5,
  output out_9,
  output out_12,
  output out_15,
  output out_18,
  output out_19
);

  wire and_1_out, and_2_out, and_3_out, and_4_out, and_5_out, and_6_out, and_7_out, and_8_out, and_9_out,
       and_10_out, or_2_out, or_3_out, or_4_out, xor_1_out, xor_3_out, xor_5_out, xor_7_out, xor_9_out;

  and and_1 (and_1_out, in_2, in_1);
  or or_1 (out_5, and_2_out, and_1_out);
  and and_2 (and_2_out, in_3, xor_1_out);
  xor xor_1 (xor_1_out, in_2, in_1);
  xor xor_2 (out_4, xor_1_out, in_3);
  and and_3 (and_3_out, in_7, in_6);
  and and_4 (and_4_out, in_11, in_10);
  and and_5 (and_5_out, in_14, in_13);
  and and_6 (and_6_out, in_17, in_16);
  or or_2 (or_2_out, and_7_out, and_3_out);
  or or_3 (or_3_out, and_8_out, and_4_out);
  or or_4 (or_4_out, and_9_out, and_5_out);
  or or_5 (out_19, and_10_out, and_6_out);
  and and_7 (and_7_out, in_8, xor_3_out);
  and and_8 (and_8_out, or_2_out, xor_5_out);
  and and_9 (and_9_out, or_3_out, xor_7_out);
  and and_10 (and_10_out, or_4_out, xor_9_out);
  xor xor_3 (xor_3_out, in_7, in_6);
  xor xor_4 (out_9, xor_3_out, in_8);
  xor xor_5 (xor_5_out, in_11, in_10);
  xor xor_6 (out_12, xor_5_out, or_2_out);
  xor xor_7 (xor_7_out, in_14, in_13);
  xor xor_8 (out_15, xor_7_out, or_3_out);
  xor xor_9 (xor_9_out, in_17, in_16);
  xor xor_10 (out_18, xor_9_out, or_4_out);
  Seven_Seg_Hex seven_seg_hex_1 (.d({out_18, out_15, out_12, out_9}), .dp(1'b0));

  // Notes on the sheet:
  //   Carry-out
  //   Carry-in
  //   A
  //   Output
  //   B
  //   A_0
  //   S_0
  //   A_1
  //   S_1
  //   A_2
  //   S_2
  //   A_3
  //   S_3
  //   B_0
  //   B_1
  //   B_2
  //   B_3
  //   overflow
endmodule
